// Logisim project 2.circ as structural Verilog
module sel2_1bit (
  input  C1,
  input  C2,
  input  SEL,
  output Y
);

  wire and_1_out, and_2_out, not_1_out;

  not not_1 (not_1_out, SEL);
  and and_1 (and_1_out, C1, not_1_out);
  and and_2 (and_2_out, SEL, C2);
  or or_1 (Y, and_1_out, and_2_out);
endmodule

module sel2_4bit (
  input  C1,
  input  C2,
  input  C3,
  input  C4,
  input  SEL1,
  input  SEL0,
  output Y
);

  wire and_1_out, and_2_out, and_3_out, and_4_out, not_1_out, not_2_out, not_3_out, not_4_out;

  not not_1 (not_1_out, SEL1);
  not not_2 (not_2_out, SEL0);
  not not_3 (not_3_out, SEL1);
  not not_4 (not_4_out, SEL0);
  and and_1 (and_1_out, C1, not_1_out, not_2_out);
  and and_2 (and_2_out, C2, not_3_out, SEL0);
  and and_3 (and_3_out, C3, SEL1, not_4_out);
  and and_4 (and_4_out, C4, SEL1, SEL0);
  or or_1 (Y, and_1_out, and_2_out, and_3_out, and_4_out);
endmodule

module HALF_ADDER (
  input  A,
  input  B,
  output sum,
  output carry
);

  xor xor_1 (sum, A, B);
  and and_1 (carry, A, B);
endmodule

module FULL_ADDER (
  input  A,
  input  B,
  input  ci,
  output sum,
  output cout
);

  wire and_1_out, and_2_out, xor_1_out;

  xor xor_1 (xor_1_out, A, B);
  xor xor_2 (sum, xor_1_out, ci);
  and and_1 (and_1_out, xor_1_out, ci);
  and and_2 (and_2_out, A, B);
  or or_1 (cout, and_1_out, and_2_out);
endmodule

module ADDER_4bit (
  input  A3,
  input  A2,
  input  A1,
  input  A0,
  input  B3,
  input  B2,
  input  B1,
  input  B0,
  output Z3,
  output Z2,
  output Z1,
  output Z0,
  output overflow
);

  wire full_adder_1_cout, full_adder_2_cout, half_adder_1_carry;

  HALF_ADDER half_adder_1 (.A(A0), .B(B0), .sum(Z0), .carry(half_adder_1_carry));
  FULL_ADDER full_adder_1 (.A(A1), .B(B1), .ci(half_adder_1_carry), .sum(Z1), .cout(full_adder_1_cout));
  FULL_ADDER full_adder_2 (.A(A2), .B(B2), .ci(full_adder_1_cout), .sum(Z2), .cout(full_adder_2_cout));
  FULL_ADDER full_adder_3 (.A(A3), .B(B3), .ci(full_adder_2_cout), .sum(Z3), .cout(overflow));
endmodule

module COMPARATOR_2bit (
  input  X1,
  input  X0,
  input  Y1,
  input  Y0,
  output C,
  output ZR
);

  wire and_1_out, and_2_out, and_3_out, and_4_out, and_5_out, and_6_out;

  and and_1 (and_1_out, X1, ~Y1);  // AND_Gate
  and and_2 (and_2_out, X0, ~Y0, ~Y1);  // AND_Gate
  and and_3 (and_3_out, X1, X0, ~Y0);  // AND_Gate
  and and_4 (and_4_out, Y1, ~X1);  // AND_Gate
  and and_5 (and_5_out, Y0, ~X1, ~X0);  // AND_Gate
  and and_6 (and_6_out, Y1, Y0, ~X0);  // AND_Gate
  or or_1 (C, and_1_out, and_2_out, and_3_out);
  or or_2 (ZR, and_4_out, and_5_out, and_6_out);
endmodule

module ALU_4bit (
  input  [3:0] A,
  input  [3:0] B,
  input  OP2,
  input  OP3,
  input  OP1,
  output Z3,
  output Z2,
  output Z1,
  output Z0
);

  wire and_1_out, and_2_out, and_3_out, and_4_out, not_1_out, not_2_out, not_3_out, not_4_out, or_1_out,
       or_2_out, or_3_out, or_4_out, tAdderZ0, tAdderZ1, tAdderZ2, tAdderZ3, tLogicZ0, tLogicZ1, tLogicZ2,
       tLogicZ3, xor_1_out, xor_2_out, xor_3_out, xor_4_out;

  and and_1 (and_1_out, A[3], B[3]);
  or or_1 (or_1_out, A[3], B[3]);
  xor xor_1 (xor_1_out, A[3], B[3]);
  not not_1 (not_1_out, A[3]);
  and and_2 (and_2_out, A[2], B[2]);
  or or_2 (or_2_out, A[2], B[2]);
  xor xor_2 (xor_2_out, A[2], B[2]);
  not not_2 (not_2_out, A[2]);
  and and_3 (and_3_out, A[1], B[1]);
  or or_3 (or_3_out, A[1], B[1]);
  xor xor_3 (xor_3_out, A[1], B[1]);
  not not_3 (not_3_out, A[1]);
  and and_4 (and_4_out, A[0], B[0]);
  or or_4 (or_4_out, A[0], B[0]);
  xor xor_4 (xor_4_out, A[0], B[0]);
  not not_4 (not_4_out, A[0]);
  sel2_4bit sel2_4bit_1 (
    .C1(and_1_out), .C2(or_1_out), .C3(xor_1_out), .C4(not_1_out), .SEL1(OP2), .SEL0(OP3), .Y(tLogicZ3));
  sel2_4bit sel2_4bit_2 (
    .C1(and_2_out), .C2(or_2_out), .C3(xor_2_out), .C4(not_2_out), .SEL1(OP2), .SEL0(OP3), .Y(tLogicZ2));
  sel2_4bit sel2_4bit_3 (
    .C1(and_3_out), .C2(or_3_out), .C3(xor_3_out), .C4(not_3_out), .SEL1(OP2), .SEL0(OP3), .Y(tLogicZ1));
  sel2_4bit sel2_4bit_4 (
    .C1(and_4_out), .C2(or_4_out), .C3(xor_4_out), .C4(not_4_out), .SEL1(OP2), .SEL0(OP3), .Y(tLogicZ0));
  sel2_1bit sel2_1bit_1 (.C1(tLogicZ3), .C2(tAdderZ3), .SEL(OP1), .Y(Z3));
  sel2_1bit sel2_1bit_2 (.C1(tLogicZ2), .C2(tAdderZ2), .SEL(OP1), .Y(Z2));
  sel2_1bit sel2_1bit_3 (.C1(tLogicZ1), .C2(tAdderZ1), .SEL(OP1), .Y(Z1));
  sel2_1bit sel2_1bit_4 (.C1(tLogicZ0), .C2(tAdderZ0), .SEL(OP1), .Y(Z0));
  ADDER_4bit adder_4bit_1 (
    .A3(A[3]), .A2(A[2]), .A1(A[1]), .A0(A[0]), .B3(B[3]), .B2(B[2]), .B1(B[1]), .B0(B[0]), .Z3(tAdderZ3),
    .Z2(tAdderZ2), .Z1(tAdderZ1), .Z0(tAdderZ0));  // open: overflow

  // Other names for the same wires on the sheet: tA0 = A[0]; tA1 = A[1]; tA2 = A[2]; tA3 = A[3]; tB0 = B[0];
  //   tB1 = B[1]; tB2 = B[2]; tB3 = B[3]
endmodule
