// Logisim project 3.circ as structural Verilog
module SEL2_1bit (
  input  C1,
  input  C2,
  input  SEL,
  output Y
);

  wire and_1_out, and_2_out, not_1_out;

  not not_1 (not_1_out, SEL);
  and and_1 (and_1_out, C1, not_1_out);
  and and_2 (and_2_out, SEL, C2);
  or or_1 (Y, and_1_out, and_2_out);
endmodule

module DFF (
);

  wire button_1_out, button_2_out, d_ff_1_q, not_1_out;

  Button button_1 (.out(button_1_out));
  Button button_2 (.out(button_2_out));
  not not_1 (not_1_out, d_ff_1_q);
  D_Flip_Flop d_ff_1 (.D(not_1_out), .clk(button_1_out), .Q(d_ff_1_q), .reset(button_2_out));  // open: Qn, preset
  LED led_1 (.in(d_ff_1_q));
endmodule

module DFF_Selector (
  input  SEL,
  output Dout
);

  wire button_1_out, button_2_out, d_ff_1_q, not_1_out;

  Button button_1 (.out(button_1_out));
  Button button_2 (.out(button_2_out));
  D_Flip_Flop d_ff_1 (.D(Dout), .clk(button_1_out), .Q(d_ff_1_q), .reset(button_2_out));  // open: Qn, preset
  not not_1 (not_1_out, d_ff_1_q);
  SEL2_1bit sel2_1bit_1 (.C1(d_ff_1_q), .C2(not_1_out), .SEL(SEL), .Y(Dout));
endmodule

module DFF_Arbitrary (
  input  val,
  input  I,
  input  SEL1,
  output Dout
);

  wire button_1_out, button_2_out, d_ff_1_q, not_1_out, sel2_1bit_1_y;

  SEL2_1bit sel2_1bit_1 (.C1(Dout), .C2(val), .SEL(I), .Y(sel2_1bit_1_y));
  Button button_1 (.out(button_1_out));
  Button button_2 (.out(button_2_out));
  D_Flip_Flop d_ff_1 (.D(sel2_1bit_1_y), .clk(button_1_out), .Q(d_ff_1_q), .reset(button_2_out));  // open: Qn, preset
  not not_1 (not_1_out, d_ff_1_q);
  SEL2_1bit sel2_1bit_2 (.C1(d_ff_1_q), .C2(not_1_out), .SEL(SEL1), .Y(Dout));
endmodule
