// Logisim project 4.circ as structural Verilog
module SEL_2 (
  input  C1,
  input  C2,
  input  SEL,
  output Y
);

  wire and_1_out, and_2_out, not_1_out;

  not not_1 (not_1_out, SEL);
  and and_1 (and_1_out, C1, not_1_out);
  and and_2 (and_2_out, SEL, C2);
  or or_1 (Y, and_1_out, and_2_out);
endmodule

module SEL_4 (
  input  C1,
  input  C2,
  input  C3,
  input  C4,
  input  SEL1,
  input  SEL0,
  output Y
);

  wire and_1_out, and_2_out, and_3_out, and_4_out, not_1_out, not_2_out, not_3_out, not_4_out;

  not not_1 (not_1_out, SEL1);
  not not_2 (not_2_out, SEL0);
  not not_3 (not_3_out, SEL1);
  not not_4 (not_4_out, SEL0);
  and and_1 (and_1_out, C1, not_1_out, not_2_out);
  and and_2 (and_2_out, C2, not_3_out, SEL0);
  and and_3 (and_3_out, C3, SEL1, not_4_out);
  and and_4 (and_4_out, C4, SEL1, SEL0);
  or or_1 (Y, and_1_out, and_2_out, and_3_out, and_4_out);
endmodule

module REG_Transmission (
);

  wire B_q, button_1_out;

  Button button_1 (.out(button_1_out));
  D_Flip_Flop A (.D(B_q), .clk(button_1_out));  // open: Q, Qn, preset, reset
  D_Flip_Flop B (.D(B_q), .clk(button_1_out), .Q(B_q));  // open: Qn, preset, reset

  // Notes on the sheet:
  //   A register: 1
  //   B register:1
  //   command: cp
endmodule

module REG_Transmission_fromA (
);

  wire A_q, button_1_out;

  Button button_1 (.out(button_1_out));
  D_Flip_Flop A (.D(A_q), .clk(button_1_out), .Q(A_q));  // open: Qn, preset, reset
  D_Flip_Flop B (.D(A_q), .clk(button_1_out));  // open: Q, Qn, preset, reset
endmodule

module REG_Switch (
  input  RST,
  input  SEL1,
  input  SEL2,
  input  SEL3
);

  wire button_1_out, d_ff_1_q, d_ff_2_q, sel_2_1_y, sel_2_2_y, sel_2_3_y;

  Button button_1 (.out(button_1_out));
  SEL_2 sel_2_1 (.C1(d_ff_1_q), .C2(sel_2_3_y), .SEL(SEL1), .Y(sel_2_1_y));
  SEL_2 sel_2_2 (.C1(d_ff_2_q), .C2(sel_2_3_y), .SEL(SEL2), .Y(sel_2_2_y));
  D_Flip_Flop d_ff_1 (.D(sel_2_1_y), .clk(button_1_out), .Q(d_ff_1_q), .reset(RST));  // open: Qn, preset
  D_Flip_Flop d_ff_2 (.D(sel_2_2_y), .clk(button_1_out), .Q(d_ff_2_q), .reset(RST));  // open: Qn, preset
  SEL_2 sel_2_3 (.C1(d_ff_1_q), .C2(d_ff_2_q), .SEL(SEL3), .Y(sel_2_3_y));

  // Other names for the same wires on the sheet: tRST = RST
endmodule

module REG_4 (
  input  SEL1,
  input  SEL2,
  input  SEL5_1,
  input  SEL5_2,
  input  SEL3,
  input  SEL4
);

  wire regA_q, regB_q, regC_q, regD_q, sel_2_1_y, sel_2_2_y, sel_2_3_y, sel_2_4_y, sel_4_1_y, tCLK, tRST;

  Button button_1 (.out(tRST));
  Button button_2 (.out(tCLK));
  SEL_2 sel_2_1 (.C1(regA_q), .C2(sel_4_1_y), .SEL(SEL1), .Y(sel_2_1_y));
  SEL_2 sel_2_2 (.C1(regB_q), .C2(sel_4_1_y), .SEL(SEL2), .Y(sel_2_2_y));
  SEL_2 sel_2_3 (.C1(regC_q), .C2(sel_4_1_y), .SEL(SEL3), .Y(sel_2_3_y));
  SEL_2 sel_2_4 (.C1(regD_q), .C2(sel_4_1_y), .SEL(SEL4), .Y(sel_2_4_y));
  D_Flip_Flop regA (.D(sel_2_1_y), .clk(tCLK), .Q(regA_q), .reset(tRST));  // open: Qn, preset
  D_Flip_Flop regB (.D(sel_2_2_y), .clk(tCLK), .Q(regB_q), .reset(tRST));  // open: Qn, preset
  D_Flip_Flop regC (.D(sel_2_3_y), .clk(tCLK), .Q(regC_q), .reset(tRST));  // open: Qn, preset
  D_Flip_Flop regD (.D(sel_2_4_y), .clk(tCLK), .Q(regD_q), .reset(tRST));  // open: Qn, preset
  SEL_4 sel_4_1 (.C1(regA_q), .C2(regB_q), .C3(regC_q), .C4(regD_q), .SEL1(SEL5_1), .SEL0(SEL5_2), .Y(sel_4_1_y));
endmodule
