// Logisim project class_report_bp21042.circ as structural Verilog: 20 circuits, main circuit main
module main (
  input  CLOCK,
  input  [2:0] OP,
  input  [3:0] \const ,
  input  SEL4_1,
  input  SEL1_1,
  input  SEL4_0,
  input  SEL1_0,
  input  SEL2_1,
  input  SEL6_1,
  input  SEL2_0,
  input  SEL5_1,
  input  SEL6_0,
  input  SEL5_0,
  input  SEL3_1,
  input  SEL3_0,
  output out_16
);

  wire tRST;
  wire [3:0] alu_4_1_z, sel4_4_1_y, sel4_4_2_y, sel4_4_3_y, sel4_4_4_y, sel4_4_5_y, sel4_4_6_y, tR0, tR1, tR2;

  Button button_1 (.out(tRST));
  Hex_Digit_Display hex_digit_display_1 (.value(tR0));  // open: dp
  SEL4_4 sel4_4_1 (.C1(tR0), .C2(sel4_4_6_y), .C3(\const ), .SEL1(SEL1_1), .SEL0(SEL1_0), .Y(sel4_4_1_y));  // open: C4
  SEL4_4 sel4_4_2 (.C1(tR1), .C2(sel4_4_6_y), .C3(\const ), .SEL1(SEL2_1), .SEL0(SEL2_0), .Y(sel4_4_2_y));  // open: C4
  SEL4_4 sel4_4_3 (.C1(tR2), .C2(sel4_4_6_y), .C3(\const ), .SEL1(SEL3_1), .SEL0(SEL3_0), .Y(sel4_4_3_y));  // open: C4
  Hex_Digit_Display hex_digit_display_2 (.value(tR1));  // open: dp
  Hex_Digit_Display hex_digit_display_3 (.value(tR2));  // open: dp
  REG4_4 regA (.D(sel4_4_1_y), .CLOCK(CLOCK), .RESET(tRST), .Q(tR0));
  REG4_4 regB (.D(sel4_4_2_y), .CLOCK(CLOCK), .RESET(tRST), .Q(tR1));
  REG4_4 regC (.D(sel4_4_3_y), .CLOCK(CLOCK), .RESET(tRST), .Q(tR2));
  SEL4_4 sel4_4_4 (.C1(tR0), .C2(tR1), .C3(tR2), .SEL1(SEL4_1), .SEL0(SEL4_0), .Y(sel4_4_4_y));  // open: C4
  SEL4_4 sel4_4_5 (.C1(tR0), .C2(tR1), .C3(tR2), .SEL1(SEL5_1), .SEL0(SEL5_0), .Y(sel4_4_5_y));  // open: C4
  ALU_4 alu_4_1 (.A(sel4_4_4_y), .B(sel4_4_5_y), .OP(OP), .Z(alu_4_1_z), .C(out_16));  // open: ZR
  SEL4_4 sel4_4_6 (.C1(tR0), .C2(tR1), .C3(tR2), .C4(alu_4_1_z), .SEL1(SEL6_1), .SEL0(SEL6_0), .Y(sel4_4_6_y));

  // Other names for the same wires on the sheet: CZR = out_16; tCLK = CLOCK
endmodule

module sel2_1 (
  input  C1,
  input  C2,
  input  SEL,
  output Y
);

  wire and_1_out, and_2_out, not_1_out;

  not not_1 (not_1_out, SEL);
  and and_1 (and_1_out, C1, not_1_out);
  and and_2 (and_2_out, SEL, C2);
  or or_1 (Y, and_1_out, and_2_out);
endmodule

module sel4_1 (
  input  C1,
  input  C2,
  input  C3,
  input  C4,
  input  SEL1,
  input  SEL0,
  output Y
);

  wire and_1_out, and_2_out, and_3_out, and_4_out;

  and and_1 (and_1_out, C1, ~SEL1, ~SEL0);  // AND_Gate
  and and_2 (and_2_out, C2, ~SEL1, SEL0);  // AND_Gate
  and and_3 (and_3_out, C3, SEL1, ~SEL0);  // AND_Gate
  and and_4 (and_4_out, C4, SEL1, SEL0);
  or or_1 (Y, and_1_out, and_2_out, and_3_out, and_4_out);
endmodule

module SEL4_4 (
  input  [3:0] C1,
  input  [3:0] C2,
  input  [3:0] C3,
  input  [3:0] C4,
  input  SEL1,
  input  SEL0,
  output [3:0] Y
);

  wire [3:0] and_1_out, and_2_out, and_3_out, and_4_out;

  assign and_1_out = C1 & ~{4{SEL1}} & ~{4{SEL0}};  // AND_Gate and_1, 4 bits wide
  assign and_2_out = C2 & ~{4{SEL1}} & {4{SEL0}};  // AND_Gate and_2, 4 bits wide
  assign and_3_out = C3 & {4{SEL1}} & ~{4{SEL0}};  // AND_Gate and_3, 4 bits wide
  assign and_4_out = C4 & {4{SEL1}} & {4{SEL0}};  // AND_Gate and_4, 4 bits wide
  assign Y = and_1_out | and_2_out | and_3_out | and_4_out;  // OR_Gate or_1, 4 bits wide
endmodule

module HALF_ADDER (
  input  A,
  input  B,
  output sum,
  output carry
);

  xor xor_1 (sum, A, B);
  and and_1 (carry, A, B);
endmodule

module FULL_ADDER (
  input  A,
  input  B,
  input  ci,
  output sum,
  output cout
);

  wire and_1_out, and_2_out, xor_1_out;

  xor xor_1 (xor_1_out, A, B);
  xor xor_2 (sum, xor_1_out, ci);
  and and_1 (and_1_out, xor_1_out, ci);
  and and_2 (and_2_out, A, B);
  or or_1 (cout, and_1_out, and_2_out);
endmodule

module ADDER_4 (
  input  A3,
  input  A2,
  input  A1,
  input  A0,
  input  B3,
  input  B2,
  input  B1,
  input  B0,
  output Z3,
  output Z2,
  output Z1,
  output Z0,
  output overflow
);

  wire full_adder_1_cout, full_adder_2_cout, half_adder_1_carry;

  HALF_ADDER half_adder_1 (.A(A0), .B(B0), .sum(Z0), .carry(half_adder_1_carry));
  FULL_ADDER full_adder_1 (.A(A1), .B(B1), .ci(half_adder_1_carry), .sum(Z1), .cout(full_adder_1_cout));
  FULL_ADDER full_adder_2 (.A(A2), .B(B2), .ci(full_adder_1_cout), .sum(Z2), .cout(full_adder_2_cout));
  FULL_ADDER full_adder_3 (.A(A3), .B(B3), .ci(full_adder_2_cout), .sum(Z3), .cout(overflow));
endmodule

module COMPARATOR_2 (
  input  X1,
  input  X0,
  input  Y1,
  input  Y0,
  output C,
  output ZR
);

  wire and_1_out, and_2_out, and_3_out, and_4_out, and_5_out, and_6_out;

  and and_1 (and_1_out, X1, ~Y1);  // AND_Gate
  and and_2 (and_2_out, X0, ~Y0, ~Y1);  // AND_Gate
  and and_3 (and_3_out, X1, X0, ~Y0);  // AND_Gate
  and and_4 (and_4_out, Y1, ~X1);  // AND_Gate
  and and_5 (and_5_out, Y0, ~X1, ~X0);  // AND_Gate
  and and_6 (and_6_out, Y1, Y0, ~X0);  // AND_Gate
  or or_1 (C, and_1_out, and_2_out, and_3_out);
  or or_2 (ZR, and_4_out, and_5_out, and_6_out);
endmodule

module COMPARATOR_4 (
  input  X3,
  input  X2,
  input  X1,
  input  X0,
  input  Y3,
  input  Y2,
  input  Y1,
  input  Y0,
  output C,
  output ZR
);

  wire and_1_out, and_2_out, comparator_2_1_c, comparator_2_1_zr, comparator_2_2_c, comparator_2_2_zr;

  COMPARATOR_2 comparator_2_1 (.X1(X3), .X0(X2), .Y1(Y3), .Y0(Y2), .C(comparator_2_1_c), .ZR(comparator_2_1_zr));
  COMPARATOR_2 comparator_2_2 (.X1(X1), .X0(X0), .Y1(Y1), .Y0(Y0), .C(comparator_2_2_c), .ZR(comparator_2_2_zr));
  and and_1 (and_1_out, ~comparator_2_1_c, ~comparator_2_1_zr, comparator_2_2_c);  // AND_Gate
  and and_2 (and_2_out, ~comparator_2_1_c, ~comparator_2_1_zr, comparator_2_2_zr);  // AND_Gate
  or or_1 (C, comparator_2_1_c, and_1_out);
  or or_2 (ZR, and_2_out, comparator_2_1_zr);
endmodule

module ALU_1 (
  input  A,
  input  B,
  input  SEL2,
  input  SEL3,
  output out_5
);

  wire and_1_out, not_1_out, or_1_out, xor_1_out;

  and and_1 (and_1_out, A, B);
  or or_1 (or_1_out, A, B);
  xor xor_1 (xor_1_out, A, B);
  not not_1 (not_1_out, A);
  sel4_1 sel4_1_1 (.C1(and_1_out), .C2(or_1_out), .C3(xor_1_out), .C4(not_1_out), .SEL1(SEL2), .SEL0(SEL3), .Y(out_5));
endmodule

module ALU_4 (
  input  [3:0] A,
  input  [3:0] B,
  input  [2:0] OP,
  output [3:0] Z,
  output C,
  output ZR
);

  wire adder_4_1_overflow, and_1_out, and_2_out, and_3_out, and_4_out, and_5_out, and_6_out, and_7_out,
       and_8_out, comparator_4_1_c, comparator_4_1_zr, nor_1_out, not_1_out, not_2_out, not_3_out, not_4_out,
       or_1_out, or_2_out, or_3_out, or_4_out, tAdderZ0, tAdderZ1, tAdderZ2, tAdderZ3, tLogicZ0, tLogicZ1,
       tLogicZ2, tLogicZ3, xor_1_out, xor_2_out, xor_3_out, xor_4_out;

  and and_1 (and_1_out, A[3], B[3]);
  or or_1 (or_1_out, A[3], B[3]);
  xor xor_1 (xor_1_out, A[3], B[3]);
  not not_1 (not_1_out, A[3]);
  and and_2 (and_2_out, A[2], B[2]);
  or or_2 (or_2_out, A[2], B[2]);
  xor xor_2 (xor_2_out, A[2], B[2]);
  not not_2 (not_2_out, A[2]);
  and and_3 (and_3_out, A[1], B[1]);
  or or_3 (or_3_out, A[1], B[1]);
  xor xor_3 (xor_3_out, A[1], B[1]);
  not not_3 (not_3_out, A[1]);
  and and_4 (and_4_out, A[0], B[0]);
  or or_4 (or_4_out, A[0], B[0]);
  xor xor_4 (xor_4_out, A[0], B[0]);
  not not_4 (not_4_out, A[0]);
  sel4_1 sel4_1_1 (
    .C1(and_1_out), .C2(or_1_out), .C3(xor_1_out), .C4(not_1_out), .SEL1(OP[1]), .SEL0(OP[0]), .Y(tLogicZ3));
  sel4_1 sel4_1_2 (
    .C1(and_2_out), .C2(or_2_out), .C3(xor_2_out), .C4(not_2_out), .SEL1(OP[1]), .SEL0(OP[0]), .Y(tLogicZ2));
  sel4_1 sel4_1_3 (
    .C1(and_3_out), .C2(or_3_out), .C3(xor_3_out), .C4(not_3_out), .SEL1(OP[1]), .SEL0(OP[0]), .Y(tLogicZ1));
  sel4_1 sel4_1_4 (
    .C1(and_4_out), .C2(or_4_out), .C3(xor_4_out), .C4(not_4_out), .SEL1(OP[1]), .SEL0(OP[0]), .Y(tLogicZ0));
  COMPARATOR_4 comparator_4_1 (
    .X3(A[3]), .X2(A[2]), .X1(A[1]), .X0(A[0]), .Y3(B[3]), .Y2(B[2]), .Y1(B[1]), .Y0(B[0]),
    .C(comparator_4_1_c), .ZR(comparator_4_1_zr));
  nor nor_1 (nor_1_out, tAdderZ3, tAdderZ2, tAdderZ1, tAdderZ0);
  sel2_1 sel2_1_1 (.C1(tLogicZ3), .C2(tAdderZ3), .SEL(OP[2]), .Y(Z[3]));
  sel2_1 sel2_1_2 (.C1(tLogicZ2), .C2(tAdderZ2), .SEL(OP[2]), .Y(Z[2]));
  sel2_1 sel2_1_3 (.C1(tLogicZ1), .C2(tAdderZ1), .SEL(OP[2]), .Y(Z[1]));
  sel2_1 sel2_1_4 (.C1(tLogicZ0), .C2(tAdderZ0), .SEL(OP[2]), .Y(Z[0]));
  ADDER_4 adder_4_1 (
    .A3(A[3]), .A2(A[2]), .A1(A[1]), .A0(A[0]), .B3(B[3]), .B2(B[2]), .B1(B[1]), .B0(B[0]), .Z3(tAdderZ3),
    .Z2(tAdderZ2), .Z1(tAdderZ1), .Z0(tAdderZ0), .overflow(adder_4_1_overflow));
  and and_5 (and_5_out, OP[2], ~OP[1], OP[0], adder_4_1_overflow);  // AND_Gate
  and and_6 (and_6_out, OP[2], OP[1], ~OP[0], comparator_4_1_c);  // AND_Gate
  and and_7 (and_7_out, OP[2], ~OP[1], OP[0], nor_1_out);  // AND_Gate
  and and_8 (and_8_out, OP[2], OP[1], ~OP[0], comparator_4_1_zr);  // AND_Gate
  or or_5 (C, and_5_out, and_6_out);
  or or_6 (ZR, and_7_out, and_8_out);

  // Other names for the same wires on the sheet: tA0 = A[0]; tA1 = A[1]; tA2 = A[2]; tA3 = A[3]; tB0 = B[0];
  //   tB1 = B[1]; tB2 = B[2]; tB3 = B[3]; top3 = OP[0]; top2 = OP[1]; top1 = OP[2]
endmodule

module reg_exp1 (
  input  Din,
  input  in_2,
  input  val,
  input  SEL2,
  input  SEL1,
  output out_6,
  output Dout
);

  wire button_1_out, button_2_out, button_3_out, button_4_out, button_5_out, button_6_out, CLOCK_out,
       d_ff_1_q, d_ff_2_q, d_ff_3_q, d_ff_4_q, not_1_out, not_2_out, not_3_out, RESET_out, sel2_1_1_y;

  Button CLOCK (.out(CLOCK_out));
  Button RESET (.out(RESET_out));
  not not_1 (not_1_out, d_ff_1_q);
  D_Flip_Flop d_ff_1 (.D(not_1_out), .clk(button_1_out), .Q(d_ff_1_q), .reset(button_2_out));  // open: Qn, preset
  Button button_1 (.out(button_1_out));
  Button button_2 (.out(button_2_out));
  D_Flip_Flop d_ff_2 (.D(Din), .clk(CLOCK_out), .Q(d_ff_2_q), .reset(RESET_out));  // open: Qn, preset
  LED led_1 (.in(d_ff_1_q));
  sel2_1 sel2_1_1 (.C1(Dout), .C2(val), .SEL(SEL2), .Y(sel2_1_1_y));
  LED led_2 (.in(d_ff_2_q));
  D_Flip_Flop d_ff_3 (.D(sel2_1_1_y), .clk(button_3_out), .Q(d_ff_3_q), .reset(button_4_out));  // open: Qn, preset
  Button button_3 (.out(button_3_out));
  Button button_4 (.out(button_4_out));
  D_Flip_Flop d_ff_4 (.D(out_6), .clk(button_5_out), .Q(d_ff_4_q), .reset(button_6_out));  // open: Qn, preset
  Button button_5 (.out(button_5_out));
  Button button_6 (.out(button_6_out));
  not not_2 (not_2_out, d_ff_3_q);
  not not_3 (not_3_out, d_ff_4_q);
  sel2_1 sel2_1_2 (.C1(d_ff_4_q), .C2(not_3_out), .SEL(in_2), .Y(out_6));
  sel2_1 sel2_1_3 (.C1(d_ff_3_q), .C2(not_2_out), .SEL(SEL1), .Y(Dout));
endmodule

module REG_Transmission (
);

  wire B_q, button_1_out;

  Button button_1 (.out(button_1_out));
  D_Flip_Flop A (.D(B_q), .clk(button_1_out));  // open: Q, Qn, preset, reset
  D_Flip_Flop B (.D(B_q), .clk(button_1_out), .Q(B_q));  // open: Qn, preset, reset
endmodule

module REG_Transmission_fromA (
);

  wire A_q, button_1_out;

  Button button_1 (.out(button_1_out));
  D_Flip_Flop A (.D(A_q), .clk(button_1_out), .Q(A_q));  // open: Qn, preset, reset
  D_Flip_Flop B (.D(A_q), .clk(button_1_out));  // open: Q, Qn, preset, reset
endmodule

module REG_Switch (
  input  RST,
  input  SEL1,
  input  SEL2,
  input  SEL3
);

  wire button_1_out, d_ff_1_q, d_ff_2_q, sel2_1_1_y, sel2_1_2_y, sel2_1_3_y;

  Button button_1 (.out(button_1_out));
  sel2_1 sel2_1_1 (.C1(d_ff_1_q), .C2(sel2_1_3_y), .SEL(SEL1), .Y(sel2_1_1_y));
  sel2_1 sel2_1_2 (.C1(d_ff_2_q), .C2(sel2_1_3_y), .SEL(SEL2), .Y(sel2_1_2_y));
  D_Flip_Flop d_ff_1 (.D(sel2_1_1_y), .clk(button_1_out), .Q(d_ff_1_q), .reset(RST));  // open: Qn, preset
  D_Flip_Flop d_ff_2 (.D(sel2_1_2_y), .clk(button_1_out), .Q(d_ff_2_q), .reset(RST));  // open: Qn, preset
  sel2_1 sel2_1_3 (.C1(d_ff_1_q), .C2(d_ff_2_q), .SEL(SEL3), .Y(sel2_1_3_y));

  // Other names for the same wires on the sheet: tRST = RST
endmodule

module REG_4 (
  input  SEL1,
  input  SEL2,
  input  SEL5_1,
  input  SEL5_2,
  input  SEL3,
  input  SEL4
);

  wire regA_q, regB_q, regC_q, regD_q, sel2_1_1_y, sel2_1_2_y, sel2_1_3_y, sel2_1_4_y, sel4_1_1_y, tCLK, tRST;

  Button button_1 (.out(tRST));
  Button button_2 (.out(tCLK));
  sel2_1 sel2_1_1 (.C1(regA_q), .C2(sel4_1_1_y), .SEL(SEL1), .Y(sel2_1_1_y));
  sel2_1 sel2_1_2 (.C1(regB_q), .C2(sel4_1_1_y), .SEL(SEL2), .Y(sel2_1_2_y));
  sel2_1 sel2_1_3 (.C1(regC_q), .C2(sel4_1_1_y), .SEL(SEL3), .Y(sel2_1_3_y));
  sel2_1 sel2_1_4 (.C1(regD_q), .C2(sel4_1_1_y), .SEL(SEL4), .Y(sel2_1_4_y));
  D_Flip_Flop regA (.D(sel2_1_1_y), .clk(tCLK), .Q(regA_q), .reset(tRST));  // open: Qn, preset
  D_Flip_Flop regB (.D(sel2_1_2_y), .clk(tCLK), .Q(regB_q), .reset(tRST));  // open: Qn, preset
  D_Flip_Flop regC (.D(sel2_1_3_y), .clk(tCLK), .Q(regC_q), .reset(tRST));  // open: Qn, preset
  D_Flip_Flop regD (.D(sel2_1_4_y), .clk(tCLK), .Q(regD_q), .reset(tRST));  // open: Qn, preset
  sel4_1 sel4_1_1 (.C1(regA_q), .C2(regB_q), .C3(regC_q), .C4(regD_q), .SEL1(SEL5_1), .SEL0(SEL5_2), .Y(sel4_1_1_y));
endmodule

module REG4_4 (
  input  [3:0] D,
  input  CLOCK,
  input  RESET,
  output [3:0] Q
);

  D_Flip_Flop d_ff_1 (.D(D[0]), .clk(CLOCK), .Q(Q[0]), .reset(RESET));  // open: Qn, preset
  D_Flip_Flop d_ff_2 (.D(D[1]), .clk(CLOCK), .Q(Q[1]), .reset(RESET));  // open: Qn, preset
  D_Flip_Flop d_ff_3 (.D(D[2]), .clk(CLOCK), .Q(Q[2]), .reset(RESET));  // open: Qn, preset
  D_Flip_Flop d_ff_4 (.D(D[3]), .clk(CLOCK), .Q(Q[3]), .reset(RESET));  // open: Qn, preset

  // Other names for the same wires on the sheet: tCLK = CLOCK; tRST = RESET
endmodule

module enshu (
  input  [2:0] OP,
  input  SEL6_1,
  input  SEL6_0,
  input  [3:0] \const ,
  input  SEL1_1,
  input  SEL4_1,
  input  SEL1_0,
  input  SEL4_0,
  input  SEL2_1,
  input  SEL2_0,
  input  SEL5_1,
  input  SEL5_0,
  input  SEL3_1,
  input  SEL3_0
);

  wire tCLK, tRST;
  wire [3:0] alu_4_1_z, regA_q, regB_q, regC_q, sel4_4_1_y, sel4_4_2_y, sel4_4_3_y, sel4_4_4_y, sel4_4_5_y,
       sel4_4_6_y;

  Button button_1 (.out(tRST));
  Button button_2 (.out(tCLK));
  SEL4_4 sel4_4_1 (
    .C1(regA_q), .C2(sel4_4_6_y), .C3(\const ), .SEL1(SEL1_1), .SEL0(SEL1_0), .Y(sel4_4_1_y));  // open: C4
  SEL4_4 sel4_4_2 (
    .C1(regB_q), .C2(sel4_4_6_y), .C3(\const ), .SEL1(SEL2_1), .SEL0(SEL2_0), .Y(sel4_4_2_y));  // open: C4
  SEL4_4 sel4_4_3 (
    .C1(regC_q), .C2(sel4_4_6_y), .C3(\const ), .SEL1(SEL3_1), .SEL0(SEL3_0), .Y(sel4_4_3_y));  // open: C4
  REG4_4 regA (.D(sel4_4_1_y), .CLOCK(tCLK), .RESET(tRST), .Q(regA_q));
  REG4_4 regB (.D(sel4_4_2_y), .CLOCK(tCLK), .RESET(tRST), .Q(regB_q));
  REG4_4 regC (.D(sel4_4_3_y), .CLOCK(tCLK), .RESET(tRST), .Q(regC_q));
  SEL4_4 sel4_4_4 (.C1(regA_q), .C2(regB_q), .C3(regC_q), .SEL1(SEL4_1), .SEL0(SEL4_0), .Y(sel4_4_4_y));  // open: C4
  SEL4_4 sel4_4_5 (.C1(regA_q), .C2(regB_q), .C3(regC_q), .SEL1(SEL5_1), .SEL0(SEL5_0), .Y(sel4_4_5_y));  // open: C4
  ALU_4 alu_4_1 (.A(sel4_4_4_y), .B(sel4_4_5_y), .OP(OP), .Z(alu_4_1_z));  // open: C, ZR
  SEL4_4 sel4_4_6 (.C1(regA_q), .C2(regB_q), .C3(regC_q), .C4(alu_4_1_z), .SEL1(SEL6_1), .SEL0(SEL6_0), .Y(sel4_4_6_y));
endmodule

module instdec (
  input  l3,
  input  l2,
  input  l1,
  input  l0,
  output SEL1_1,
  output SEL1_0,
  output SEL2_1,
  output SEL2_0,
  output SEL3_1,
  output SEL3_0,
  output SEL4_1,
  output SEL4_0,
  output SEL5_1,
  output SEL5_0,
  output SEL6_1,
  output SEL6_0,
  output OP1,
  output OP2,
  output OP3
);

  wire and_1_out, and_2_out, and_3_out, and_4_out, and_5_out, and_6_out, and_7_out, and_8_out, and_9_out;

  and and_1 (and_1_out, ~l1, l0);  // AND_Gate
  and and_2 (and_2_out, l3, ~l1);  // AND_Gate
  and and_3 (and_3_out, ~l3, ~l2, l1);  // AND_Gate
  and and_4 (and_4_out, l3, l2);
  and and_5 (and_5_out, l3, l1);
  and and_6 (and_6_out, l3, ~l1);  // AND_Gate
  and and_7 (and_7_out, ~l3, l1, l0);  // AND_Gate
  and and_8 (and_8_out, l3, ~l2, ~l1);  // AND_Gate
  and and_9 (and_9_out, ~l3, l1, ~l0);  // AND_Gate
  and and_10 (SEL1_1, ~l3, ~l2, l1, l0);  // AND_Gate
  or or_1 (SEL1_0, and_1_out, l2, l3);
  and and_11 (SEL2_1, l2, ~l1, ~l0);  // AND_Gate
  and and_12 (SEL4_0, ~l2, ~l1, l0);  // AND_Gate
  or or_2 (SEL5_0, l0, l2);
  or or_3 (SEL6_1, l2, l3);
  or or_4 (SEL6_0, l0, l2, l3);
  or or_5 (OP1, and_4_out, and_5_out);
  or or_6 (OP2, and_6_out, and_7_out);
  or or_7 (OP3, and_8_out, and_9_out);
  or or_8 (SEL2_0, and_2_out, and_3_out);

  assign SEL3_0 = 1'b0;
  assign SEL3_1 = 1'b0;
  assign SEL4_1 = 1'b0;
  assign SEL5_1 = 1'b0;
endmodule

module DECODR (
  input  [3:0] \const ,
  input  [3:0] OP,
  output out_3
);

  wire SEL1_0, SEL1_1, SEL2_0, SEL2_1, SEL3_0, SEL3_1, SEL4_0, SEL4_1, SEL5_0, SEL5_1, SEL6_0, SEL6_1, tCLK,
       tRST;
  wire [2:0] op_t;
  wire [3:0] alu_4_1_z, sel4_4_1_y, sel4_4_2_y, sel4_4_3_y, sel4_4_4_y, sel4_4_5_y, sel4_4_6_y, tR0, tR1, tR2;

  Button button_1 (.out(tRST));
  Clock clock_1 (.out(tCLK));
  Hex_Digit_Display hex_digit_display_1 (.value(tR0));  // open: dp
  SEL4_4 sel4_4_1 (.C1(tR0), .C2(sel4_4_6_y), .C3(\const ), .SEL1(SEL1_1), .SEL0(SEL1_0), .Y(sel4_4_1_y));  // open: C4
  SEL4_4 sel4_4_2 (.C1(tR1), .C2(sel4_4_6_y), .C3(\const ), .SEL1(SEL2_1), .SEL0(SEL2_0), .Y(sel4_4_2_y));  // open: C4
  SEL4_4 sel4_4_3 (.C1(tR2), .C2(sel4_4_6_y), .C3(\const ), .SEL1(SEL3_1), .SEL0(SEL3_0), .Y(sel4_4_3_y));  // open: C4
  Hex_Digit_Display hex_digit_display_2 (.value(tR1));  // open: dp
  Hex_Digit_Display hex_digit_display_3 (.value(tR2));  // open: dp
  REG4_4 regA (.D(sel4_4_1_y), .CLOCK(tCLK), .RESET(tRST), .Q(tR0));
  REG4_4 regB (.D(sel4_4_2_y), .CLOCK(tCLK), .RESET(tRST), .Q(tR1));
  REG4_4 regC (.D(sel4_4_3_y), .CLOCK(tCLK), .RESET(tRST), .Q(tR2));
  SEL4_4 sel4_4_4 (.C1(tR0), .C2(tR1), .C3(tR2), .SEL1(SEL4_1), .SEL0(SEL4_0), .Y(sel4_4_4_y));  // open: C4
  SEL4_4 sel4_4_5 (.C1(tR0), .C2(tR1), .C3(tR2), .SEL1(SEL5_1), .SEL0(SEL5_0), .Y(sel4_4_5_y));  // open: C4
  instdec instdec_1 (
    .l3(OP[3]), .l2(OP[2]), .l1(OP[1]), .l0(OP[0]), .SEL1_1(SEL1_1), .SEL1_0(SEL1_0), .SEL2_1(SEL2_1),
    .SEL2_0(SEL2_0), .SEL3_1(SEL3_1), .SEL3_0(SEL3_0), .SEL4_1(SEL4_1), .SEL4_0(SEL4_0), .SEL5_1(SEL5_1),
    .SEL5_0(SEL5_0), .SEL6_1(SEL6_1), .SEL6_0(SEL6_0), .OP1(op_t[0]), .OP2(op_t[1]), .OP3(op_t[2]));
  ALU_4 alu_4_1 (.A(sel4_4_4_y), .B(sel4_4_5_y), .OP(op_t), .Z(alu_4_1_z), .C(out_3));  // open: ZR
  SEL4_4 sel4_4_6 (.C1(tR0), .C2(tR1), .C3(tR2), .C4(alu_4_1_z), .SEL1(SEL6_1), .SEL0(SEL6_0), .Y(sel4_4_6_y));

  // Other names for the same wires on the sheet: CZR = out_3
endmodule
